# Fritzing sketch Air_Quality (saved by Fritzing 0.9.0b)
breadboards: 1

parts:
  U1 = Sharp Dust Sensor [part_number=GP2Y1010AU0F]
  R4 = Resistor [tolerance=±5% resistance=10k package=THT]
  R5 = Resistor [tolerance=±5% resistance=18k package=THT]
  R3 = Resistor [tolerance=±5% resistance=18k package=THT]
  RHT1 = Humidity and Temperature Sensor RHT03
  C1 = Electrolytic Capacitor [capacitance=1μF package="0405 [SMD, electrolytic]"]
  Part5 = 5v Step-Up Board
  Part4 = MQ-135 breakout
  R6 = Vertical Resistor [tolerance=±5% resistance=220 package=THT]
  R1 = Resistor [tolerance=±5% resistance=220 package=THT]
  R2 = Vertical Resistor [tolerance=±5% resistance=220 package=THT]
  U2 = ESP32S-HiLetgo [part_number=ESP32S-HiLetgo]

nets:
  N1: U1.V-LED, C1.+
  GND: U1.LED-GND, U1.S-GND, C1.-, Part5.GND, U2.GND
  N2: U1.Vo, R2.Pin_1
  N3: R4.Pin_0, Part4.AO
  N4: R4.Pin_1, R5.Pin_0
  N5: R3.Pin_0, R2.Pin_0
  N6: RHT1.Vcc, R6.Pin_1, U2.3.3
  N7: RHT1.Data-signal, U2.GPIO14
  N8: RHT1.GND_2, Part4.GND
  N9: Part5.VOUT, Part4.VCC, R1.Pin_0

custom parts:
  Sharp Dust Sensor: Sharp GP2Y1010AU0F Dust Sensor
  Humidity and Temperature Sensor RHT03: Digital relative humidity & temperature sensor RHT03
  5v Step-Up Board: Description: The NCP1400 is a 3.3V DC-DC converter. The breakout board will accept voltage inputs between 1 and 3 Volts (such as 1 or 2 AA batteries) and output a constant, low ripple 3.3V output capable of sourcing up to 100 mA. This board is great for supplying power to 3.3V sensors or providing 3.3V from a a single AA battery. The breakout board includes the necessary peripheral components.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
  Vertical Resistor: A generic resistor (0.25W)
  ESP32S-HiLetgo: HiLetgo ESP-WROOM-32 ESP32 ESP-32S Development Board 2.4GHz Dual-Mode WiFi + Bluetooth Dual Cores Microcontroller The ESP32 integrated with Antenna switches, RF Balun, power amplifiers, low-noise amplifiers, filters, and management modules, and the entire solution occupies the least area of PCB. 2.4 GHz Wi-Fi plus Bluetooth dual-mode chip, with TSMC Ultra-low power consumption 40nm technology,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
